# Fritzing sketch smart patate (saved by Fritzing 0.9.3b)
breadboards: 1

parts:
  Composant1 = Arduino Uno (Rev3)
  R1 = Resistor [tolerance=±5% resistance=10k package="0603 [SMD]"]
  R2 = Resistor [tolerance=±5% resistance=3.3k package="0805 [SMD]"]
  L1 = Inductor [inductance=10mH package="400 mil [THT]"]
  D1 = Rectifier Diode [part_number=1N4148 package="300 mil [THT]"]
  R3 = Resistor [tolerance=±5% resistance=1M package=THT]
  C2 = Electrolytic Capacitor [capacitance=10nF package="100 mil [THT, electrolytic]"]
  C3 = Ceramic Capacitor [capacitance=0.1nF package="100 mil [THT, multilayer]"]
  R4 = Resistor [tolerance=±5% resistance=160 package=THT]
  R5 = Resistor [tolerance=±5% resistance=160 package=THT]
  LED1 = LED - 5mm [color="Red (633nm)" package="5 mm [THT]"]
  LED2 = LED - 5mm [color="Green (570nm)" package="5 mm [THT]"]

nets:
  N1: Composant1.A0, D1.anode, R3.Pin_0, C3.0
  N2: Composant1.D9_PWM, R1.Pin_0
  N3: Composant1.D6_PWM, R5.Pin_0
  N4: Composant1.D7, R4.Pin_0
  N5: Composant1.GND, R2.Pin_1, R3.Pin_1, C3.1, LED1.anode, LED2.anode
  N6: R1.Pin_1, R2.Pin_0, L1.pin_0
  N7: L1.pin_1, D1.cathode, C2.+
  N8: R4.Pin_1, LED2.cathode
  N9: R5.Pin_1, LED1.cathode
